# Fritzing sketch schema (saved by Fritzing 0.9.3b)

parts:
  U1 = LuaNode32 / ESP32
  SIM800L_BO1 = SIM800L BO
  C1 = Capacitor Polarized [package=panasonic_d]
  Součástka1 = Solar Cell
  Součástka2 = INA219 High Side DC Current Sensor Breakout [part_number=904]
  U4 = MPC1700 [package=sot23-3]
  C2 = Electrolytic Capacitor [capacitance=1000μF package="1010 [SMD, electrolytic]"]
  C3 = Capacitor [package=cap-pth-small2]
  Součástka3 = Adafruit SHT31-D Sensirion Temperature/Humidity Sensor [part_number="Adafruit #2857"]
  Součástka4 = Adafruit SHT31-D Sensirion Temperature/Humidity Sensor [part_number="Adafruit #2857"]
  Součástka5 = Adafruit SHT31-D Sensirion Temperature/Humidity Sensor [part_number="Adafruit #2857"]
  Součástka6 = Adafruit MMA8451 Accelerometer [part_number="Adafruit #2019"]
  Součástka7 = Adafruit MMA8451 Accelerometer [part_number="Adafruit #2019"]
  Součástka8 = Adafruit MMA8451 Accelerometer [part_number="Adafruit #2019"]
  S1 = Reed switch [package=THT]
  S2 = Reed switch [package=THT]
  S3 = Reed switch [package=THT]
  Součástka10 = GY-BMEP280 Barometric Pressure Sensor - Breakout
  Součástka11 = Adafruit MAX4466 Electret Microphone Amplifier [part_number="Adafruit #1063"]
  Součástka12 = Adafruit MAX4466 Electret Microphone Amplifier [part_number="Adafruit #1063"]
  Součástka13 = Adafruit MAX4466 Electret Microphone Amplifier [part_number="Adafruit #1063"]
  Q1 = Basic FET N-Channel [package="TO220 [THT]"]
  Part1 = Solar Charge Controller [part_number="HGX Series Solar Charge Controller PWM" package=PWM-Model]
  VCC1 = Battery block 9V
  Součástka14 = INA219 High Side DC Current Sensor Breakout [part_number=904]

nets:
  N1: U1.D32, Součástka11.VCC
  N2: U1.D33, Součástka13.VCC
  N3: U1.D25, S3.pin_1
  N4: U1.D26, S1.pin_1
  N5: U1.D27, S2.pin_1
  N6: U1.D14, Součástka6.SA0
  N7: U1.D12, Součástka8.SA0
  N8: U1.D13, Součástka7.SA0
  GND: U1.GND, Součástka2.GND, U4.GND, C2.-, C3.1, Součástka3.GND, Součástka4.GND, Součástka5.GND, Součástka6.GND, Součástka7.GND, Součástka8.GND, Součástka10.GND, Součástka11.GND, Součástka12.GND, Součástka13.GND, Q1.source, Part1.Connector_6, Součástka14.GND
  VIN: U1.3V3, Součástka2.VCC, U4.OUT, Součástka3.VIN, Součástka4.VIN, Součástka5.VIN, Součástka6.VIN, Součástka7.VIN, Součástka8.VIN, S1.pin_2, S2.pin_2, S3.pin_2, Součástka10.VCC, Součástka14.VCC
  N9: U1.D15, U1.D2, Q1.gate
  N10: U1.D4, U1.RX2, SIM800L_BO1.pin_5
  N11: U1.TX2, SIM800L_BO1.pin_4
  N12: U1.D5, Součástka5.ADDR
  N13: U1.D18, Součástka4.ADDR, Součástka4.RST
  N14: U1.D19, Součástka3.ADDR
  N15: U1.D21, Součástka1.+, Součástka2.VIN+, Součástka2.SDA, Součástka3.SDA, Součástka4.SDA, Součástka5.SDA, Součástka6.SDA, Součástka7.SDA, Součástka8.SDA, Součástka10.SDA, Part1.Connector_3, Součástka14.VIN-, Součástka14.SDA
  N16: U1.TX0, U1.D22, Součástka2.VIN-, Součástka2.SCL, Součástka3.SCL, Součástka4.SCL, Součástka5.SCL, Součástka6.SCL, Součástka7.SCL, Součástka7.INT1, Součástka8.SCL, Součástka10.SCL, Part1.Connector_1, Součástka14.SCL
  N17: U1.D23, Součástka12.VCC
  N18: SIM800L_BO1.PIN2, C1.+
  N19: SIM800L_BO1.PIN3, Q1.drain
  N20: SIM800L_BO1.pin_6, C1.-
  N21: SIM800L_BO1.pin_9, Součástka11.OUT, Součástka12.OUT, Součástka13.OUT
  N22: Součástka1.-, Part1.Connector_2
  N23: U4.IN, C2.+, C3.2, Part1.Connector_5
  N24: Part1.Connector_4, VCC1.-
  N25: VCC1.+, Součástka14.VIN+

notes:
  MAX4466 MIC sensors
  vin, gnd, scl, sda, temp addr, gyro addr, mic vin, mic out
  18V 40W solar panel
  12V 55Ah battery
  12V -> 3.3V
  Magnetic lock sensors
  MMA8452Q gyroscope sensors
  INA219 sensors
  SHT31 temperature/humidity sensors
  BMP280 temperature/humidity/presure sensor

custom parts:
  LuaNode32 / ESP32: ESP32 based LuaNode32
  INA219 High Side DC Current Sensor Breakout: This breakout board will solve all your power-monitoring problems. Instead of struggling with two multimeters, you can just use the handy INA219B chip on this breakout to both measure both the high side voltage and DC current draw over I2C with 1% precision. Most current-measuring devices such as our current panel meter are only good for low side measuring. That means that unless you want to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
  MPC1700: Small package LDO
  Adafruit SHT31-D Sensirion Temperature/Humidity Sensor: Sensirion Temperature/Humidity sensors are some of the finest & highest-accuracy devices you can get. And, finally we have some that have a true I2C interface for easy reading. The SHT31-D sensor has an excellent ±2% relative humidity and ±0.3°C accuracy for most uses. Unlike earlier SHT sensors, this sensor has a true I2C interface, and (bonus!) even with two address options. It also is 3V or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
  Adafruit MMA8451 Accelerometer: So many accelerometers and so little time! We've expanded our accelerometer selection even more with this high-precision and inexpensive MMA8451 Triple-Axis Accelerometer w/ 14-bit ADC. You can detect motion, tilt and basic orientation with a digital accelerometer - and the MMA8451 is a great accelerometer to start with. It has a wide usage range, from +-2g up to +-8g yet is easy to use with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
  GY-BMEP280 Barometric Pressure Sensor - Breakout: The BME280 is a chip which was originally designed for the next generation of smartphones. It is made up of a very accurate pressure sensor and an associated temperature sensor which helps calibrate the pressure readings. And just for fun they threw in a pretty solid humidity sensor in there as well! So with an I2C connection you have access to enough weather data to make some pretty good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
  Adafruit MAX4466 Electret Microphone Amplifier: Add an ear to your project with this well-designed electret microphone amplifier. This fully assembled and tested board comes with a 20-20KHz electret microphone soldered on. For the amplification, we use the Maxim MAX4466, an op-amp specifically designed for this delicate task! The amplifier has excellent power supply noise rejection, so this amplifier sounds really good and isn't nearly as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
  Solar Charge Controller: PWM-Solar Charge Controller
